# Fritzing sketch soil_sensor (saved by Fritzing 0.9.3b)

parts:
  Part1 = Adafruit Circuit Playground Express [part_number="Adafruit #3333"]
  Part2 = Adafruit STEMMA Soil Sensor - I2C Capacitive Moisture Sensor [part_number="Adafruit #4026"]

nets:
  3.3V: Part1.3.3V, Part2.VIN
  GND: Part1.GND, Part2.GND
  N1: Part1.D3_A4_SCL, Part2.SCL
  N2: Part1.D2_A5_SDA, Part2.SDA

custom parts:
  Adafruit Circuit Playground Express: Circuit Playground Express is the next step towards a perfect introduction to electronics and programming. We've taken the original Circuit Playground Classic and made it even better! Not only did we pack even more sensors in, we also made it even easier to program. You can now start your journey with Microsoft MakeCode block-based or Javascript programming. Then, you can use the same board to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
  Adafruit STEMMA Soil Sensor - I2C Capacitive Moisture Sensor: Most low cost soil sensors are resistive style, where there's two prongs and the sensor measures the conductivity between the two. These work OK at first, but eventually start to oxidize because of the exposed metal. Even if they're gold plated! The resistivity measurement goes up and up, so you constantly have to re-calibrate your code. Also, resistive measurements don't always work in loose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
